// Logisim project control-logic.circ as structural Verilog: 1 circuit, main circuit control_logic
module control_logic (
  input  [31:0] Instruction,
  input  BrEq,
  input  BrLt,
  output PCSel,
  output RegWEn,
  output [2:0] ImmSel,
  output BrUn,
  output ASel,
  output BSel,
  output [3:0] ALUSel,
  output MemWEn,
  output [1:0] WBSel
);

  wire and_1_out, and_3_out, and_4_out, and_13_out, and_14_out, and_15_out, and_16_out, and_17_out,
       and_18_out, comparator_1_eq, comparator_2_eq, comparator_3_eq, comparator_4_eq, comparator_5_eq,
       comparator_6_eq, comparator_7_eq, comparator_8_eq, comparator_14_eq, comparator_19_eq, isB, IsBeq,
       IsBge, IsBgeu, IsBlt, IsBltu, IsBne, isI, isIStar, isJ, isJalr, isLoad, isLui, isMul, isR, isRSub,
       isSpecial, isU, not_1_out, not_2_out, not_3_out, not_4_out, not_5_out, not_6_out, not_7_out, or_2_out,
       or_3_out, or_5_out, or_6_out;
  wire [1:0] multiplexer_3_out;
  wire [2:0] multiplexer_7_out, multiplexer_8_out, multiplexer_9_out, multiplexer_10_out, multiplexer_12_out;
  wire [3:0] adder_1_out, bit_extender_1_out, IALU, multiplexer_1_out, multiplexer_5_out, multiplexer_6_out,
       multiplexer_11_out, multiplexer_13_out;
  wire [15:0] rom_1_data;

  not not_1 (not_1_out, Instruction[13]);
  Comparator #(.width(3)) comparator_1 (.a(Instruction[14:12]), .b(3'b000), .eq(comparator_1_eq));  // open: gt, lt
  not not_2 (not_2_out, comparator_2_eq);
  Comparator #(.mode("unsigned"), .width(7)) comparator_2 (
    .a(Instruction[31:25]), .b({7{1'b0}}), .eq(comparator_2_eq));  // open: gt, lt
  Comparator #(.mode("unsigned"), .width(3)) comparator_3 (
    .a(Instruction[14:12]), .b(3'b000), .eq(comparator_3_eq));  // open: gt, lt
  Comparator #(.mode("unsigned"), .width(3)) comparator_4 (
    .a(Instruction[14:12]), .b(3'b101), .eq(comparator_4_eq));  // open: gt, lt
  Comparator #(.mode("unsigned"), .width(3)) comparator_5 (
    .a(Instruction[14:12]), .b(3'b111), .eq(comparator_5_eq));  // open: gt, lt
  Comparator #(.mode("unsigned"), .width(3)) comparator_6 (
    .a(Instruction[14:12]), .b(3'b100), .eq(comparator_6_eq));  // open: gt, lt
  Comparator #(.mode("unsigned"), .width(3)) comparator_7 (
    .a(Instruction[14:12]), .b(3'b110), .eq(comparator_7_eq));  // open: gt, lt
  Comparator #(.mode("unsigned"), .width(3)) comparator_8 (
    .a(Instruction[14:12]), .b(3'b001), .eq(comparator_8_eq));  // open: gt, lt
  Comparator #(.mode("unsigned"), .width(7)) comparator_9 (
    .a(Instruction[6:0]), .b(7'b0100011), .eq(MemWEn));  // open: gt, lt
  Comparator #(.mode("unsigned"), .width(7)) comparator_10 (
    .a(Instruction[6:0]), .b(7'b0000011), .eq(isLoad));  // open: gt, lt
  Comparator #(.mode("unsigned"), .width(7)) comparator_11 (
    .a(Instruction[6:0]), .b(7'b0010011), .eq(isI));  // open: gt, lt
  and and_1 (and_1_out, Instruction[12], not_1_out);
  Comparator #(.mode("unsigned"), .width(7)) comparator_12 (
    .a(Instruction[6:0]), .b(7'b0110011), .eq(isR));  // open: gt, lt
  and and_2 (isRSub, isR, comparator_1_eq, comparator_14_eq);
  and and_3 (and_3_out, isIStar, not_2_out);
  and and_4 (and_4_out, isR, not_2_out);
  Comparator #(.mode("unsigned"), .width(7)) comparator_13 (
    .a(Instruction[6:0]), .b(7'b1100011), .eq(isB));  // open: gt, lt
  and and_5 (BrUn, isB, Instruction[13]);
  and and_6 (IsBeq, isB, comparator_3_eq);
  and and_7 (IsBge, isB, comparator_4_eq);
  and and_8 (IsBgeu, isB, comparator_5_eq);
  and and_9 (IsBlt, isB, comparator_6_eq);
  and and_10 (IsBltu, isB, comparator_7_eq);
  and and_11 (IsBne, isB, comparator_8_eq);
  ROM #(.addrWidth(6), .dataWidth(16)) rom_1 (.data(rom_1_data));  // open: addr
  and and_12 (isIStar, isI, and_1_out);
  or or_1 (isSpecial, and_3_out, and_4_out);
  assign bit_extender_1_out = {{1{1'b0}}, Instruction[14:12]};  // Bit_Extender bit_extender_1
  Comparator #(.mode("unsigned"), .width(7)) comparator_14 (
    .a(Instruction[31:25]), .b(7'b0100000), .eq(comparator_14_eq));  // open: gt, lt
  Adder #(.width(4)) adder_1 (.a(bit_extender_1_out), .b(4'b1000), .out(adder_1_out));  // open: cin, cout
  not not_3 (not_3_out, BrLt);
  not not_4 (not_4_out, BrEq);
  Comparator #(.mode("unsigned"), .width(7)) comparator_15 (
    .a(Instruction[6:0]), .b(7'b1101111), .eq(isJ));  // open: gt, lt
  Comparator #(.mode("unsigned"), .width(7)) comparator_16 (
    .a(Instruction[6:0]), .b(7'b0010111), .eq(isU));  // open: gt, lt
  Comparator #(.mode("unsigned"), .width(7)) comparator_17 (
    .a(Instruction[6:0]), .b(7'b0110111), .eq(isLui));  // open: gt, lt
  Comparator #(.mode("unsigned"), .width(7)) comparator_18 (
    .a(Instruction[6:0]), .b(7'b1100111), .eq(isJalr));  // open: gt, lt
  Multiplexer #(.width(4)) multiplexer_1 (
    .in0(bit_extender_1_out), .in1(adder_1_out), .out(multiplexer_1_out), .sel(or_2_out));
  or or_2 (or_2_out, isSpecial, isMul);
  and and_13 (and_13_out, IsBeq, BrEq);
  and and_14 (and_14_out, IsBge, not_3_out);
  and and_15 (and_15_out, IsBgeu, not_3_out);
  and and_16 (and_16_out, IsBlt, BrLt);
  and and_17 (and_17_out, IsBltu, BrLt);
  and and_18 (and_18_out, IsBne, not_4_out);
  Multiplexer #(.width(4)) multiplexer_2 (.in0(4'b1100), .in1(multiplexer_1_out), .out(IALU), .sel(not_5_out));
  not not_5 (not_5_out, isRSub);
  or or_3 (or_3_out, and_13_out, and_14_out, and_15_out, and_16_out, and_17_out, and_18_out);
  Comparator #(.mode("unsigned"), .width(7)) comparator_19 (
    .a(Instruction[31:25]), .b(7'b0000001), .eq(comparator_19_eq));  // open: gt, lt
  and and_19 (isMul, isR, comparator_19_eq);
  or or_4 (PCSel, or_3_out, isJ, isJalr);
  Multiplexer #(.width(2)) multiplexer_3 (.in0(2'b01), .in1(2'b10), .out(multiplexer_3_out), .sel(or_5_out));
  or or_5 (or_5_out, isJ, isJalr);
  Multiplexer #(.width(2)) multiplexer_4 (.in0(multiplexer_3_out), .in1(2'b00), .out(WBSel), .sel(isLoad));
  Multiplexer #(.select(3), .width(4)) multiplexer_5 (
    .in0(IALU), .in1(4'b0000), .in2(4'b0000), .in3(4'b0000), .in4(4'b0000), .out(multiplexer_5_out),
    .sel(ImmSel));  // open: in5, in6, in7
  or or_6 (or_6_out, isU, isLui);
  Multiplexer #(.width(4)) multiplexer_6 (.in0(multiplexer_5_out), .in1(IALU), .out(multiplexer_6_out), .sel(isR));
  or or_7 (ASel, isJ, isB, isU);
  Multiplexer #(.width(3)) multiplexer_7 (.in0(3'b000), .in1(3'b001), .out(multiplexer_7_out), .sel(MemWEn));
  Multiplexer #(.width(3)) multiplexer_8 (.in0(3'b000), .in1(3'b010), .out(multiplexer_8_out), .sel(isB));
  Multiplexer #(.width(3)) multiplexer_9 (.in0(3'b000), .in1(3'b011), .out(multiplexer_9_out), .sel(or_6_out));
  Multiplexer #(.width(3)) multiplexer_10 (.in0(3'b000), .in1(3'b100), .out(multiplexer_10_out), .sel(isJ));
  Multiplexer #(.width(4)) multiplexer_11 (
    .in0(multiplexer_6_out), .in1(4'b0000), .out(multiplexer_11_out), .sel(isLoad));
  Multiplexer #(.width(3)) multiplexer_12 (.in0(3'b000), .in1(3'b000), .out(multiplexer_12_out), .sel(isI));
  Multiplexer #(.width(4)) multiplexer_13 (
    .in0(multiplexer_11_out), .in1(4'b1111), .out(multiplexer_13_out), .sel(isLui));
  not not_6 (not_6_out, MemWEn);
  not not_7 (not_7_out, isB);
  assign ImmSel = multiplexer_12_out | multiplexer_7_out | multiplexer_8_out | multiplexer_9_out | multiplexer_10_out;  // OR_Gate or_8, 3 bits wide
  Multiplexer #(.width(4)) multiplexer_14 (.in0(multiplexer_13_out), .in1(4'b0000), .out(ALUSel), .sel(isJalr));
  and and_20 (RegWEn, not_6_out, not_7_out);
  not not_8 (BSel, isR);

  // Other names for the same wires on the sheet: isS = MemWEn; opcode[6:0] = Instruction[6:0];
  //   funct3[2:0] = Instruction[14:12]; funct7[6:0] = Instruction[31:25]; RALU[3:0] = IALU

  // Notes on the sheet:
  //   INPUTS to your circuit
  //   Connect ROM Input here ->
  //   ROM FOR CONTROL LOGIC
  //   DON'T CHANGE THE LOCATIONS OF THE INPUTS AND OUTPUTS!
  //   This is only if you choose to do the ROM option
  //   CONNECT
  //   WIRE
  //   TO
  //   USE
  //   ROM
  //   OUTPUT from your circuit
  //   Reminder: If using ROM, use combinational logic for PCSel
endmodule
