// Logisim project imm-gen.circ as structural Verilog: 1 circuit, main circuit imm_gen
module imm_gen (
  input  [31:0] Instruction,
  input  [2:0] ImmSel,
  output [31:0] Immediate
);

  wire [31:0] bit_extender_2_out, BType, IType, JType, SType, UType;

  assign SType = {{20{Instruction[31]}}, {Instruction[31:25], Instruction[11:7]}};  // Bit_Extender bit_extender_1
  assign bit_extender_2_out = {{12{Instruction[31]}}, Instruction[31:12]};  // Bit_Extender bit_extender_2
  assign JType = {{11{Instruction[31]}}, {Instruction[31], Instruction[19:12], Instruction[20], Instruction[30:21], 1'b0}};  // Bit_Extender bit_extender_3
  Shifter #(.width(32)) shifter_1 (.in(bit_extender_2_out), .\dist (5'b01100), .out(UType));
  assign IType = {{20{Instruction[31]}}, Instruction[31:20]};  // Bit_Extender bit_extender_4
  assign BType = {{19{Instruction[31]}}, {Instruction[31], Instruction[7], Instruction[30:25], Instruction[11:8], 1'b0}};  // Bit_Extender bit_extender_5
  Multiplexer #(.select(3), .width(32)) multiplexer_1 (
    .in0(IType), .in1(SType), .in2(BType), .in3(UType), .in4(JType), .out(Immediate), .sel(ImmSel));  // open: in5, in6, in7

  // Notes on the sheet:
  //   INPUTS to your circuit
  //   DON'T CHANGE THE LOCATIONS OF THE INPUTS AND OUTPUTS!
  //   OUTPUT from your circuit
endmodule
