// Logisim project partial-store.circ as structural Verilog: 1 circuit, main circuit partial_store
module partial_store (
  input  [31:0] Instruction,
  input  [31:0] MemAddress,
  input  [31:0] DataFromReg,
  input  MemWEn,
  output [3:0] MemWriteMask,
  output [31:0] DataToMem
);

  wire [1:0] offset;
  wire [3:0] multiplexer_1_out, multiplexer_2_out, multiplexer_10_out;
  wire [7:0] bit_extender_1_out;
  wire [15:0] bit_extender_2_out;
  wire [31:0] sbResult, shResult;

  Bit_Extender #(.in_width(32), .out_width(8)) bit_extender_1 (.in(DataFromReg), .out(bit_extender_1_out));
  Bit_Extender #(.in_width(32)) bit_extender_2 (.in(DataFromReg), .out(bit_extender_2_out));
  Multiplexer #(.select(2), .width(4)) multiplexer_1 (
    .in0(4'b0001), .in1(4'b0010), .in2(4'b0100), .in3(4'b1000), .out(multiplexer_1_out), .sel(offset));
  Multiplexer #(.select(2), .width(4)) multiplexer_2 (
    .in0(4'b0011), .in2(4'b1100), .out(multiplexer_2_out), .sel(offset));  // open: in1, in3
  Multiplexer #(.width(8)) multiplexer_3 (
    .in0({8{1'b0}}), .in1(bit_extender_1_out), .out(sbResult[7:0]), .sel(MemWriteMask[0]));
  Multiplexer #(.width(8)) multiplexer_4 (
    .in0({8{1'b0}}), .in1(bit_extender_1_out), .out(sbResult[15:8]), .sel(MemWriteMask[1]));
  Multiplexer #(.width(8)) multiplexer_5 (
    .in0({8{1'b0}}), .in1(bit_extender_1_out), .out(sbResult[23:16]), .sel(MemWriteMask[2]));
  Multiplexer #(.width(8)) multiplexer_6 (
    .in0({8{1'b0}}), .in1(bit_extender_1_out), .out(sbResult[31:24]), .sel(MemWriteMask[3]));
  Multiplexer #(.width(16)) multiplexer_7 (
    .in0({16{1'b0}}), .in1(bit_extender_2_out), .out(shResult[15:0]), .sel(MemWriteMask[0]));
  Multiplexer #(.width(16)) multiplexer_8 (
    .in0({16{1'b0}}), .in1(bit_extender_2_out), .out(shResult[31:16]), .sel(MemWriteMask[2]));
  Multiplexer #(.select(3), .width(32)) multiplexer_9 (
    .in0(sbResult), .in1(shResult), .in2(DataFromReg), .out(DataToMem), .sel(Instruction[14:12]));  // open: in3, in4, in5, in6, in7
  Multiplexer #(.select(3), .width(4)) multiplexer_10 (
    .in0(multiplexer_1_out), .in1(multiplexer_2_out), .in2(4'b1111), .out(multiplexer_10_out),
    .sel(Instruction[14:12]));  // open: in3, in4, in5, in6, in7
  Bit_Extender #(.in_width(32), .out_width(2)) bit_extender_3 (.in(MemAddress), .out(offset));
  Multiplexer #(.width(4)) multiplexer_11 (.in0(4'b0000), .in1(multiplexer_10_out), .out(MemWriteMask), .sel(MemWEn));

  // Other names for the same wires on the sheet: func3[2:0] = Instruction[14:12]; MaskBit0 = MemWriteMask[0];
  //   MaskBit1 = MemWriteMask[1]; MaskBit2 = MemWriteMask[2]; MaskBit3 = MemWriteMask[3];
  //   swResult[31:0] = DataFromReg

  // Notes on the sheet:
  //   INPUTS to your circuit
  //   DON'T CHANGE THE LOCATIONS OF THE INPUTS AND OUTPUTS!
  //   OUTPUT from your circuit
endmodule
